# Fritzing sketch Freezer (saved by Fritzing 0.5.2b)
breadboards: 3

parts:
  OUT1 = Stereo Jack (TRS) 3.5mm [package="PG203J [THT]"]
  OUT5 = Stereo Jack (TRS) 3.5mm [package="PG203J [THT]"]
  OUT8 = Stereo Jack (TRS) 3.5mm [package="PG203J [THT]"]
  OUT4 = Stereo Jack (TRS) 3.5mm [package="PG203J [THT]"]
  OUT2 = Stereo Jack (TRS) 3.5mm [package="PG203J [THT]"]
  OUT7 = Stereo Jack (TRS) 3.5mm [package="PG203J [THT]"]
  OUT3 = Stereo Jack (TRS) 3.5mm [package="PG203J [THT]"]
  OUT6 = Stereo Jack (TRS) 3.5mm [package="PG203J [THT]"]
  LTV847 = IC, DIP package, 16 pins [chip_label=LTV847 spacing=300mil]
  LTV847_2 = IC, DIP package, 16 pins [chip_label=LTV847 spacing=300mil]
  LTV847_3 = IC, DIP package, 16 pins [chip_label=LTV847 spacing=300mil]
  LTV847_4 = IC, DIP package, 16 pins [chip_label=LTV847 spacing=300mil]
  Resistors = IC, DIP package, 16 pins [chip_label=Resistor spacing=300mil]
  74HC595 = 74HC595 [package="DIP16 [THT]"]
  Arduino_Nano_3_0 = Arduino Nano v2.3
  74HC595_2 = 74HC595 [package="DIP16 [THT]"]
  Resistors_2 = IC, DIP package, 16 pins [chip_label=Resistor spacing=300mil]
  J1 = Screw terminal - 2 pins [package=THT]
  R2 = Resistor [resistance=220 package=THT]
  IN1 = Stereo Jack (TRS) 3.5mm [package="PG203J [THT]"]
  J2 = screw terminal, 5 pins
  J3 = screw terminal, 11 pins

nets:
  N1: OUT1.Sleeve, LTV847_3.pin14, LTV847_3.pin16
  N2: OUT1.Ring, LTV847_3.pin13
  N3: OUT1.Tip, LTV847_3.pin15
  N4: OUT5.Sleeve, LTV847.pin14, LTV847.pin16
  N5: OUT5.Ring, LTV847.pin13
  N6: OUT5.Tip, LTV847.pin15
  N7: OUT8.Sleeve, LTV847_2.pin10, LTV847_2.pin12
  N8: OUT8.Ring, LTV847_2.pin9
  N9: OUT8.Tip, LTV847_2.pin11
  N10: OUT4.Sleeve, LTV847_4.pin10, LTV847_4.pin12
  N11: OUT4.Ring, LTV847_4.pin9
  N12: OUT4.Tip, LTV847_4.pin11
  N13: OUT2.Sleeve, LTV847_3.pin10, LTV847_3.pin12
  N14: OUT2.Ring, LTV847_3.pin9
  N15: OUT2.Tip, LTV847_3.pin11
  N16: OUT7.Sleeve, LTV847_2.pin14, LTV847_2.pin16
  N17: OUT7.Ring, LTV847_2.pin13
  N18: OUT7.Tip, LTV847_2.pin15
  N19: OUT3.Sleeve, LTV847_4.pin14, LTV847_4.pin16
  N20: OUT3.Ring, LTV847_4.pin13
  N21: OUT3.Tip, LTV847_4.pin15
  N22: OUT6.Sleeve, LTV847.pin10, LTV847.pin12
  N23: OUT6.Ring, LTV847.pin9
  N24: OUT6.Tip, LTV847.pin11
  N25: LTV847.pin1, Resistors_2.pin16
  GND: LTV847.pin2, LTV847.pin4, LTV847.pin6, LTV847.pin8, LTV847_2.pin2, LTV847_2.pin4, LTV847_2.pin6, LTV847_2.pin8, LTV847_3.pin2, LTV847_3.pin4, LTV847_3.pin6, LTV847_3.pin8, LTV847_4.pin2, LTV847_4.pin4, LTV847_4.pin6, LTV847_4.pin8, 74HC595.GND, Arduino_Nano_3_0.GND, 74HC595_2.GND, J1.pin2, R2.Pin_0
  N26: LTV847.pin3, Resistors_2.pin15
  N27: LTV847.pin5, Resistors_2.pin14
  N28: LTV847.pin7, Resistors_2.pin13
  N29: LTV847_2.pin1, Resistors_2.pin12
  N30: LTV847_2.pin3, Resistors_2.pin11
  N31: LTV847_2.pin5, Resistors_2.pin10
  N32: LTV847_2.pin7, Resistors_2.pin9
  N33: LTV847_3.pin1, Resistors.pin16
  N34: LTV847_3.pin3, Resistors.pin15
  N35: LTV847_3.pin5, Resistors.pin14
  N36: LTV847_3.pin7, Resistors.pin13
  N37: LTV847_4.pin1, Resistors.pin12
  N38: LTV847_4.pin3, Resistors.pin11
  N39: LTV847_4.pin5, Resistors.pin10
  N40: LTV847_4.pin7, Resistors.pin9
  N41: Resistors.pin1, 74HC595_2.Q7
  N42: Resistors.pin2, 74HC595_2.Q6
  N43: Resistors.pin3, 74HC595_2.Q5
  N44: Resistors.pin4, 74HC595_2.Q4
  N45: Resistors.pin5, 74HC595_2.Q3
  N46: Resistors.pin6, 74HC595_2.Q2
  N47: Resistors.pin7, 74HC595_2.Q1
  N48: Resistors.pin8, 74HC595_2.Q0
  N49: 74HC595.Q1, Resistors_2.pin7
  N50: 74HC595.Q2, Resistors_2.pin6
  N51: 74HC595.Q3, Resistors_2.pin5
  N52: 74HC595.Q4, Resistors_2.pin4
  N53: 74HC595.Q5, Resistors_2.pin3
  N54: 74HC595.Q6, Resistors_2.pin2
  N55: 74HC595.Q7, Resistors_2.pin1
  N56: 74HC595.Q7', 74HC595_2.DS
  N57: 74HC595.MR, Arduino_Nano_3_0.D2, 74HC595_2.MR
  N58: 74HC595.SH_CP, Arduino_Nano_3_0.D3, 74HC595_2.SH_CP
  N59: 74HC595.ST_CP, Arduino_Nano_3_0.D6, 74HC595_2.ST_CP
  N60: 74HC595.OE, Arduino_Nano_3_0.D5, 74HC595_2.OE
  N61: 74HC595.DS, Arduino_Nano_3_0.D4
  N62: 74HC595.Q0, Resistors_2.pin8
  VCC: 74HC595.VCC, Arduino_Nano_3_0.+5V, 74HC595_2.VCC, IN1.Ring, IN1.Tip
  N63: Arduino_Nano_3_0.D7, R2.Pin_1, IN1.Sleeve
  N64: Arduino_Nano_3_0.D8, J2.pin5
  N65: Arduino_Nano_3_0.D9, J2.pin4
  N66: Arduino_Nano_3_0.D10, J2.pin3
  N67: Arduino_Nano_3_0.D11, J2.pin2
  N68: Arduino_Nano_3_0.D12, J2.pin1
  N69: Arduino_Nano_3_0.D13, J3.pin11
  N70: Arduino_Nano_3_0.3V3, J3.pin10
  N71: Arduino_Nano_3_0.AREF, J3.pin9
  N72: Arduino_Nano_3_0.A7, J3.pin8
  N73: Arduino_Nano_3_0.A6, J3.pin7
  N74: Arduino_Nano_3_0.A5, J3.pin6
  N75: Arduino_Nano_3_0.A4, J3.pin5
  N76: Arduino_Nano_3_0.A3, J3.pin4
  N77: Arduino_Nano_3_0.A2, J3.pin3
  N78: Arduino_Nano_3_0.A1, J3.pin2
  N79: Arduino_Nano_3_0.A0, J3.pin1
  N80: Arduino_Nano_3_0.VIN, J1.pin1
